# Fritzing sketch schematic (saved by Fritzing 0.7.12b)
breadboards: 1

parts:
  Arduino1 = Arduino
  T1 = LM35 Temperature Sensor [package="TO92 [THT]"]
  U1 = LM 358 Dual Op-Amp [package="DIP8 [THT]"]
  R1 = 100k Ω Resistor [package=THT]
  R2 = 10k Ω Resistor [package=THT]
  R3 = Resistor [tolerance=±5% resistance=220 package="0805 [SMD]"]
  R4 = 100k Ω Resistor [package=THT]
  R5 = 100k Ω Resistor [package=THT]
  R6 = Resistor [tolerance=±5% resistance=220 package=THT]
  R7 = Resistor [tolerance=±5% resistance=220 package=THT]
  R8 = Resistor [tolerance=±5% resistance=220 package=THT]

nets:
  N1: Arduino1.D8, R6.Pin_0
  N2: Arduino1.D5, R3.Pin_0
  N3: Arduino1.D4, R5.Pin_1
  N4: Arduino1.+5V, T1.+Vs, U1.connector7
  GND: Arduino1.GND, T1.GND, U1.connector3, R2.Pin_1, R8.Pin_1
  N5: Arduino1.A0, U1.connector0, R1.Pin_0
  N6: Arduino1.A1, R4.Pin_0
  N7: T1.Vout, U1.connector2
  N8: U1.connector1, R1.Pin_1, R2.Pin_0
  N9: R4.Pin_1, R5.Pin_0
  N10: R6.Pin_1, R7.Pin_0
  N11: R7.Pin_1, R8.Pin_0

notes:
  Feuchtesensor (zwei Stiftleisten-Pins)
  WiFly-Pins:
  2 3 1 10
